// Logisim project root.circ as structural Verilog
module main (
);

  wire button_1_out, clk, controlpath_1_load, controlpath_1_store;
  wire [7:0] adder_1_out, datapath_1_address, datapath_1_dataout, ram_1_dout, register_1_q;
  wire [23:0] rom_1_data;

  Clock clock_1 (.out(clk));
  Register register_1 (.D(adder_1_out), .Q(register_1_q), .clk(clk));  // open: en, clr
  Adder adder_1 (.a(register_1_q), .b(8'h1), .out(adder_1_out));  // open: cin, cout
  ROM #(.dataWidth(24)) rom_1 (.addr(register_1_q), .data(rom_1_data));
  DataPath datapath_1 (
    .selDataIn(clk), .Address(datapath_1_address), .DataOut(datapath_1_dataout));  // open: DataIn, Params, clk, selDataOut
  ControlPath controlpath_1 (.Opcode(rom_1_data[23:16]), .Load(controlpath_1_load), .Store(controlpath_1_store));
  Button button_1 (.out(button_1_out));
  RAM #(.clearpin("true")) ram_1 (
    .addr(datapath_1_address), .we(controlpath_1_store), .oe(controlpath_1_load), .clk(clk),
    .din(datapath_1_dataout), .dout(ram_1_dout), .clr(button_1_out));

  // Notes on the sheet:
  //   contents of rom_1 (hex, n*v repeats v):
  //   440003 410000 420100 830100 410101 420201 930200
endmodule

module ControlPath (
  input  [7:0] Opcode,
  output Load,
  output Store
);
endmodule

module DataPath (
  input  [7:0] DataIn,
  input  selDataIn,
  input  [15:0] Params,
  input  clk,
  input  selDataOut,
  output [7:0] Address,
  output [7:0] DataOut
);

  wire [7:0] register_1_q;
  wire [15:0] multiplexer_1_out;
  wire [15:8] undriven, undriven_2;

  ULA ula_1 ();
  Multiplexer #(.width(16)) multiplexer_1 (
    .in0({undriven, DataIn}), .in1({undriven_2, Params[7:0]}), .out(multiplexer_1_out), .sel(selDataIn));
  Register register_1 (.D(multiplexer_1_out[7:0]), .Q(register_1_q), .clk(clk));  // open: en, clr
  Multiplexer #(.width(8)) multiplexer_2 (
    .in0(multiplexer_1_out[7:0]), .in1(register_1_q), .out(DataOut), .sel(selDataOut));
  // Pins of 8 and 16 bits meet at {undriven, DataIn}
  // Pins of 8 and 16 bits meet at {undriven_2, Params[7:0]}
  // Pins of 8 and 16 bits meet at multiplexer_1_out

  assign Address = Params[15:8];
endmodule
